// Logisim project Control Unit.circ as structural Verilog: 6 circuits, main circuit main
module main (
  input  [6:0] in_1,
  output out_2,
  output out_3,
  output out_4,
  output out_5,
  output out_6,
  output [2:0] out_7,
  output [1:0] out_8,
  output out_9,
  output [1:0] out_10,
  output [1:0] out_11
);

  wire type_decode_1_branch, type_decode_1_i_type, type_decode_1_jal, type_decode_1_jalr, type_decode_1_load,
       type_decode_1_lui, type_decode_1_r_format, type_decode_1_store;

  // Probe on in_1
  Type_Decode type_decode_1 (
    .in_1(in_1), .R_Format(type_decode_1_r_format), .Load(type_decode_1_load), .Store(type_decode_1_store),
    .Branch(type_decode_1_branch), .I_Type(type_decode_1_i_type), .JALR(type_decode_1_jalr),
    .JAL(type_decode_1_jal), .LUI(type_decode_1_lui));
  Control_Decode control_decode_1 (
    .MemWrite(out_2), .Branch_2(out_3), .MemRead(out_4), .RegWrite(out_5), .MemToReg(out_6),
    .ALU_Operation(out_7), .Operand_A_Select(out_8), .Operand_A_Select_2(out_9), .Extend_Select(out_10),
    .Next_PC_Select(out_11), .R_Format(type_decode_1_r_format), .Load(type_decode_1_load),
    .Store(type_decode_1_store), .Branch(type_decode_1_branch), .I_Type(type_decode_1_i_type),
    .JALR(type_decode_1_jalr), .JAL(type_decode_1_jal), .LUI(type_decode_1_lui));
endmodule

module Type_Decode (
  input  [6:0] in_1,
  output R_Format,
  output Load,
  output Store,
  output Branch,
  output I_Type,
  output JALR,
  output JAL,
  output LUI
);

  Comparator #(.width(7)) comparator_1 (.a(in_1), .b(7'b0110011), .eq(R_Format));  // open: gt, lt
  Comparator #(.width(7)) comparator_2 (.a(in_1), .b(7'b0000011), .eq(Load));  // open: gt, lt
  Comparator #(.width(7)) comparator_3 (.a(in_1), .b(7'b0100011), .eq(Store));  // open: gt, lt
  Comparator #(.width(7)) comparator_4 (.a(in_1), .b(7'b1100011), .eq(Branch));  // open: gt, lt
  Comparator #(.width(7)) comparator_5 (.a(in_1), .b(7'b0010011), .eq(I_Type));  // open: gt, lt
  Comparator #(.width(7)) comparator_6 (.a(in_1), .b(7'b1100111), .eq(JALR));  // open: gt, lt
  Comparator #(.width(7)) comparator_7 (.a(in_1), .b(7'b1101111), .eq(JAL));  // open: gt, lt
  Comparator #(.width(7)) comparator_8 (.a(in_1), .b(7'b0110111), .eq(LUI));  // open: gt, lt
endmodule

module Control_Decode (
  input  R_Format,
  input  Load,
  input  Store,
  input  Branch,
  input  I_Type,
  input  JALR,
  input  JAL,
  input  LUI,
  output MemWrite,
  output Branch_2,
  output MemRead,
  output RegWrite,
  output MemToReg,
  output [2:0] ALU_Operation,
  output [1:0] Operand_A_Select,
  output Operand_A_Select_2,
  output [1:0] Extend_Select,
  output [1:0] Next_PC_Select
);

  or or_1 (RegWrite, R_Format, Load, I_Type, JALR, JAL, LUI);
  ALUop aluop_1 (
    .R_Type(R_Format), .Load(Load), .Store(Store), .Branch(Branch), .I_Type(I_Type), .JALR(JALR), .JAL(JAL),
    .LUI(LUI), .out_9(ALU_Operation));
  OpA_sel opa_sel_1 (.LUI(LUI), .JALR(JALR), .JAL(JAL), .out_4(Operand_A_Select));
  or or_2 (Operand_A_Select_2, LUI, I_Type, Store, Load);
  next_pc_select next_pc_select_1 (.Branch(Branch), .JAL(JAL), .JALR(JALR), .out_4(Next_PC_Select));

  assign Branch_2 = Branch;
  assign Extend_Select = {Store, LUI};
  assign MemRead = Load;
  assign MemToReg = Load;
  assign MemWrite = Store;
endmodule

module ALUop (
  input  R_Type,
  input  Load,
  input  Store,
  input  Branch,
  input  I_Type,
  input  JALR,
  input  JAL,
  input  LUI,
  output [2:0] out_9
);

  wire not_1_out, not_2_out, not_3_out, not_4_out, not_5_out, not_6_out, not_7_out, not_8_out, not_9_out,
       not_10_out, not_11_out, not_12_out, not_13_out;

  not not_1 (not_1_out, Branch);
  not not_2 (not_2_out, R_Type);
  not not_3 (not_3_out, I_Type);
  not not_4 (not_4_out, JAL);
  not not_5 (not_5_out, JALR);
  not not_6 (not_6_out, I_Type);
  not not_7 (not_7_out, R_Type);
  not not_8 (not_8_out, Load);
  not not_9 (not_9_out, Store);
  not not_10 (not_10_out, LUI);
  not not_11 (not_11_out, R_Type);
  not not_12 (not_12_out, Branch);
  not not_13 (not_13_out, Load);
  and and_1 (out_9[2], not_1_out, not_2_out, not_3_out, not_4_out, not_5_out);
  and and_2 (out_9[1], not_6_out, not_7_out, not_8_out, not_9_out);
  and and_3 (out_9[0], not_10_out, not_11_out, not_12_out, not_13_out);
endmodule

module OpA_sel (
  input  LUI,
  input  JALR,
  input  JAL,
  output [1:0] out_4
);

  wire and_1_out, and_2_out, and_3_out, not_1_out, not_2_out, not_3_out, not_4_out, not_5_out, not_6_out,
       not_7_out, not_8_out;

  not not_1 (not_1_out, LUI);
  not not_2 (not_2_out, JALR);
  not not_3 (not_3_out, LUI);
  not not_4 (not_4_out, JAL);
  not not_5 (not_5_out, JALR);
  not not_6 (not_6_out, JAL);
  not not_7 (not_7_out, JAL);
  not not_8 (not_8_out, JALR);
  and and_1 (and_1_out, not_1_out, not_2_out, JAL);
  and and_2 (and_2_out, not_3_out, JALR, not_4_out);
  and and_3 (and_3_out, not_5_out, LUI, not_6_out);
  and and_4 (out_4[0], not_7_out, not_8_out, LUI);
  or or_1 (out_4[1], and_1_out, and_2_out, and_3_out);
endmodule

module next_pc_select (
  input  Branch,
  input  JAL,
  input  JALR,
  output [1:0] out_4
);

  wire and_1_out, and_2_out, and_3_out, and_4_out, and_5_out, not_1_out, not_2_out, not_3_out, not_4_out,
       not_5_out, not_6_out, not_7_out, not_8_out, not_9_out, not_10_out;

  not not_1 (not_1_out, Branch);
  not not_2 (not_2_out, JAL);
  not not_3 (not_3_out, Branch);
  not not_4 (not_4_out, JALR);
  not not_5 (not_5_out, JAL);
  not not_6 (not_6_out, Branch);
  not not_7 (not_7_out, Branch);
  not not_8 (not_8_out, JALR);
  not not_9 (not_9_out, JAL);
  not not_10 (not_10_out, JALR);
  and and_1 (and_1_out, not_1_out, not_2_out, JALR);
  and and_2 (and_2_out, not_3_out, JAL, not_4_out);
  and and_3 (and_3_out, not_5_out, not_6_out, JALR);
  and and_4 (and_4_out, not_7_out, JAL, not_8_out);
  and and_5 (and_5_out, Branch, not_9_out, not_10_out);
  or or_1 (out_4[1], and_1_out, and_2_out, and_3_out);
  or or_2 (out_4[0], and_4_out, and_5_out);
endmodule
