// Logisim project RV32i.circ as structural Verilog: 1 circuit, main circuit main
module main (
  input  RST
);

  wire and_1_out, clock_1_out, main_1_out_2, main_1_out_3, main_1_out_4, main_1_out_5, main_1_out_9,
       main_6_out_5;
  wire [1:0] main_1_out_8, main_1_out_10, main_1_out_11;
  wire [2:0] main_1_out_7;
  wire [4:0] main_5_out_4;
  wire [31:0] adder_1_out, main_2_readdata1, main_2_readdata2, main_3_i_immediate, main_3_s_immediate,
       main_3_sb_immediate, main_3_u_immediate, main_3_uj_type, main_4_out_3, main_6_out_4,
       multiplexer_1_out, multiplexer_2_out, multiplexer_3_out, multiplexer_4_out, multiplexer_5_out,
       multiplexer_6_out, ram_1_data, ram_2_data, register_1_q;

  Clock clock_1 (.out(clock_1_out));
  Multiplexer #(.width(32), .enable("false")) multiplexer_1 (
    .in0(adder_1_out), .in1(main_3_sb_immediate), .out(multiplexer_1_out), .sel(and_1_out));
  Multiplexer #(.select(2), .width(32), .enable("false")) multiplexer_2 (
    .in0(adder_1_out), .in1(multiplexer_1_out), .in2(main_4_out_3), .in3(main_3_uj_type),
    .out(multiplexer_2_out), .sel(main_1_out_11));
  Register #(.width(32)) register_1 (.D(multiplexer_2_out), .en(1'b1), .Q(register_1_q), .clk(clock_1_out), .clr(RST));
  Adder #(.width(32)) adder_1 (.a(32'h4), .b(register_1_q), .out(adder_1_out));  // open: cin, cout
  RAM #(.dataWidth(32)) ram_1 (
    .addr(register_1_q[7:0]), .data(ram_1_data), .sel(1'b1), .clk(clock_1_out), .ld(1'b1), .clr(RST));
  Control_Unit_main main_1 (
    .in_1(ram_1_data[6:0]), .out_2(main_1_out_2), .out_3(main_1_out_3), .out_4(main_1_out_4),
    .out_5(main_1_out_5), .out_7(main_1_out_7), .out_8(main_1_out_8), .out_9(main_1_out_9),
    .out_10(main_1_out_10), .out_11(main_1_out_11));  // open: out_6
  Reg_File_main main_2 (
    .WriteData(multiplexer_6_out), .Write_Reg(ram_1_data[11:7]), .ReadReg(main_1_out_5), .CLK(clock_1_out),
    .RST(RST), .ReadData1(main_2_readdata1), .ReadData2(main_2_readdata2), .ReadReg1(ram_1_data[19:15]),
    .ReadReg2(ram_1_data[24:20]));
  Immediate_Generation_main main_3 (
    .in_1(ram_1_data), .in_2(register_1_q), .S_Immediate(main_3_s_immediate),
    .SB_Immediate(main_3_sb_immediate), .U_Immediate(main_3_u_immediate), .UJ_Type(main_3_uj_type),
    .I_Immediate(main_3_i_immediate));
  JALR_Target_main main_4 (.in_1(register_1_q), .in_2(main_2_readdata1), .out_3(main_4_out_3));
  ALU_Control_main main_5 (
    .out_4(main_5_out_4), .ALUOp(main_1_out_7), .Func_7(ram_1_data[30]), .Func_3(ram_1_data[14:12]));
  Multiplexer #(.select(2), .width(32), .enable("false")) multiplexer_3 (
    .in0(main_3_i_immediate), .in1(main_3_u_immediate), .in2(main_3_s_immediate), .out(multiplexer_3_out),
    .sel(main_1_out_10));  // open: in3
  Multiplexer #(.select(2), .width(32), .enable("false")) multiplexer_4 (
    .in0(main_2_readdata1), .in1(register_1_q), .in2(adder_1_out), .in3({32{1'b0}}), .out(multiplexer_4_out),
    .sel(main_1_out_8));
  Multiplexer #(.width(32), .enable("false")) multiplexer_5 (
    .in0(main_2_readdata2), .in1(multiplexer_3_out), .out(multiplexer_5_out), .sel(main_1_out_9));
  ALU_main main_6 (
    .out_4(main_6_out_4), .out_5(main_6_out_5), .A(multiplexer_4_out), .B(multiplexer_5_out),
    .ALU_Control(main_5_out_4));
  Multiplexer #(.width(32), .enable("false")) multiplexer_6 (
    .in0(main_6_out_4), .in1(ram_2_data), .out(multiplexer_6_out), .sel(main_1_out_4));
  and and_1 (and_1_out, main_6_out_5, main_1_out_3);
  RAM #(.dataWidth(32), .bus("separate")) ram_2 (
    .addr(main_6_out_4[7:0]), .din(main_2_readdata2), .data(ram_2_data), .str(main_1_out_2), .sel(1'b1),
    .clk(clock_1_out), .ld(1'b1));  // open: clr
endmodule
