// Logisim project Reg File.circ as structural Verilog: 1 circuit, main circuit main
module main (
  input  [4:0] ReadReg1,
  input  [4:0] ReadReg2,
  input  [31:0] WriteData,
  input  [4:0] Write_Reg,
  input  ReadReg,
  input  CLK,
  input  RST,
  output [31:0] ReadData1,
  output [31:0] ReadData2
);

  wire decoder_1_out0, decoder_1_out1, decoder_2_out0, decoder_2_out1, decoder_2_out2, decoder_2_out3,
       decoder_3_out0, decoder_3_out1, decoder_3_out2, decoder_3_out3, decoder_4_out1, decoder_4_out2,
       decoder_4_out3, decoder_5_out0, decoder_5_out1, decoder_5_out2, decoder_5_out3, decoder_6_out0,
       decoder_6_out1, decoder_6_out2, decoder_6_out3, decoder_7_out0, decoder_7_out1, decoder_7_out2,
       decoder_7_out3, decoder_8_out0, decoder_8_out1, decoder_8_out2, decoder_8_out3, decoder_9_out0,
       decoder_9_out1, decoder_9_out2, decoder_9_out3, decoder_10_out0, decoder_10_out1, decoder_10_out2,
       decoder_10_out3, decoder_11_out0, decoder_11_out1, decoder_11_out2, decoder_11_out3;
  wire [31:0] multiplexer_1_out, multiplexer_2_out, multiplexer_3_out, multiplexer_4_out, multiplexer_5_out,
       multiplexer_6_out, multiplexer_7_out, multiplexer_8_out, multiplexer_9_out, multiplexer_10_out,
       multiplexer_11_out, multiplexer_12_out, multiplexer_13_out, multiplexer_14_out, multiplexer_15_out,
       multiplexer_16_out, multiplexer_17_out, multiplexer_18_out, multiplexer_19_out, multiplexer_20_out,
       register_1_q, register_2_q, register_3_q, register_4_q, register_5_q, register_6_q, register_7_q,
       register_8_q, register_9_q, register_10_q, register_11_q, register_12_q, register_13_q, register_14_q,
       register_15_q, register_16_q, register_17_q, register_18_q, register_19_q, register_20_q,
       register_21_q, register_22_q, register_23_q, register_24_q, register_25_q, register_26_q,
       register_27_q, register_28_q, register_29_q, register_30_q, register_31_q;

  Decoder #(.disabled(0)) decoder_1 (.out0(decoder_1_out0), .out1(decoder_1_out1), .sel(Write_Reg[4]), .en(ReadReg));
  Decoder #(.select(2), .disabled(0)) decoder_2 (
    .out0(decoder_2_out0), .out1(decoder_2_out1), .out2(decoder_2_out2), .out3(decoder_2_out3),
    .sel(Write_Reg[3:2]), .en(decoder_1_out0));
  Decoder #(.select(2), .disabled(0)) decoder_3 (
    .out0(decoder_3_out0), .out1(decoder_3_out1), .out2(decoder_3_out2), .out3(decoder_3_out3),
    .sel(Write_Reg[3:2]), .en(decoder_1_out1));
  Decoder #(.select(2), .disabled(0)) decoder_4 (
    .out1(decoder_4_out1), .out2(decoder_4_out2), .out3(decoder_4_out3), .sel(Write_Reg[1:0]),
    .en(decoder_2_out0));  // open: out0
  Decoder #(.select(2), .disabled(0)) decoder_5 (
    .out0(decoder_5_out0), .out1(decoder_5_out1), .out2(decoder_5_out2), .out3(decoder_5_out3),
    .sel(Write_Reg[1:0]), .en(decoder_2_out1));
  Decoder #(.select(2), .disabled(0)) decoder_6 (
    .out0(decoder_6_out0), .out1(decoder_6_out1), .out2(decoder_6_out2), .out3(decoder_6_out3),
    .sel(Write_Reg[1:0]), .en(decoder_2_out2));
  Decoder #(.select(2), .disabled(0)) decoder_7 (
    .out0(decoder_7_out0), .out1(decoder_7_out1), .out2(decoder_7_out2), .out3(decoder_7_out3),
    .sel(Write_Reg[1:0]), .en(decoder_2_out3));
  Decoder #(.select(2), .disabled(0)) decoder_8 (
    .out0(decoder_8_out0), .out1(decoder_8_out1), .out2(decoder_8_out2), .out3(decoder_8_out3),
    .sel(Write_Reg[1:0]), .en(decoder_3_out0));
  Decoder #(.select(2), .disabled(0)) decoder_9 (
    .out0(decoder_9_out0), .out1(decoder_9_out1), .out2(decoder_9_out2), .out3(decoder_9_out3),
    .sel(Write_Reg[1:0]), .en(decoder_3_out1));
  Decoder #(.select(2), .disabled(0)) decoder_10 (
    .out0(decoder_10_out0), .out1(decoder_10_out1), .out2(decoder_10_out2), .out3(decoder_10_out3),
    .sel(Write_Reg[1:0]), .en(decoder_3_out2));
  Decoder #(.select(2), .disabled(0)) decoder_11 (
    .out0(decoder_11_out0), .out1(decoder_11_out1), .out2(decoder_11_out2), .out3(decoder_11_out3),
    .sel(Write_Reg[1:0]), .en(decoder_3_out3));
  Register #(.width(32)) register_1 (.D(WriteData), .en(decoder_4_out1), .Q(register_1_q), .clk(CLK), .clr(RST));
  Register #(.width(32)) register_2 (.D(WriteData), .en(decoder_4_out2), .Q(register_2_q), .clk(CLK), .clr(RST));
  Register #(.width(32)) register_3 (.D(WriteData), .en(decoder_4_out3), .Q(register_3_q), .clk(CLK), .clr(RST));
  Register #(.width(32)) register_4 (.D(WriteData), .en(decoder_5_out0), .Q(register_4_q), .clk(CLK), .clr(RST));
  Register #(.width(32)) register_5 (.D(WriteData), .en(decoder_5_out1), .Q(register_5_q), .clk(CLK), .clr(RST));
  Register #(.width(32)) register_6 (.D(WriteData), .en(decoder_5_out2), .Q(register_6_q), .clk(CLK), .clr(RST));
  Register #(.width(32)) register_7 (.D(WriteData), .en(decoder_5_out3), .Q(register_7_q), .clk(CLK), .clr(RST));
  Register #(.width(32)) register_8 (.D(WriteData), .en(decoder_6_out0), .Q(register_8_q), .clk(CLK), .clr(RST));
  Register #(.width(32)) register_9 (.D(WriteData), .en(decoder_6_out1), .Q(register_9_q), .clk(CLK), .clr(RST));
  Register #(.width(32)) register_10 (.D(WriteData), .en(decoder_6_out2), .Q(register_10_q), .clk(CLK), .clr(RST));
  Register #(.width(32)) register_11 (.D(WriteData), .en(decoder_6_out3), .Q(register_11_q), .clk(CLK), .clr(RST));
  Register #(.width(32)) register_12 (.D(WriteData), .en(decoder_7_out0), .Q(register_12_q), .clk(CLK), .clr(RST));
  Register #(.width(32)) register_13 (.D(WriteData), .en(decoder_7_out1), .Q(register_13_q), .clk(CLK), .clr(RST));
  Register #(.width(32)) register_14 (.D(WriteData), .en(decoder_7_out2), .Q(register_14_q), .clk(CLK), .clr(RST));
  Register #(.width(32)) register_15 (.D(WriteData), .en(decoder_7_out3), .Q(register_15_q), .clk(CLK), .clr(RST));
  Register #(.width(32)) register_16 (.D(WriteData), .en(decoder_8_out0), .Q(register_16_q), .clk(CLK), .clr(RST));
  Register #(.width(32)) register_17 (.D(WriteData), .en(decoder_8_out1), .Q(register_17_q), .clk(CLK), .clr(RST));
  Register #(.width(32)) register_18 (.D(WriteData), .en(decoder_8_out2), .Q(register_18_q), .clk(CLK), .clr(RST));
  Register #(.width(32)) register_19 (.D(WriteData), .en(decoder_8_out3), .Q(register_19_q), .clk(CLK), .clr(RST));
  Register #(.width(32)) register_20 (.D(WriteData), .en(decoder_9_out0), .Q(register_20_q), .clk(CLK), .clr(RST));
  Register #(.width(32)) register_21 (.D(WriteData), .en(decoder_9_out1), .Q(register_21_q), .clk(CLK), .clr(RST));
  Register #(.width(32)) register_22 (.D(WriteData), .en(decoder_9_out2), .Q(register_22_q), .clk(CLK), .clr(RST));
  Register #(.width(32)) register_23 (.D(WriteData), .en(decoder_9_out3), .Q(register_23_q), .clk(CLK), .clr(RST));
  Register #(.width(32)) register_24 (.D(WriteData), .en(decoder_10_out0), .Q(register_24_q), .clk(CLK), .clr(RST));
  Register #(.width(32)) register_25 (.D(WriteData), .en(decoder_10_out1), .Q(register_25_q), .clk(CLK), .clr(RST));
  Register #(.width(32)) register_26 (.D(WriteData), .en(decoder_10_out2), .Q(register_26_q), .clk(CLK), .clr(RST));
  Register #(.width(32)) register_27 (.D(WriteData), .en(decoder_10_out3), .Q(register_27_q), .clk(CLK), .clr(RST));
  Register #(.width(32)) register_28 (.D(WriteData), .en(decoder_11_out0), .Q(register_28_q), .clk(CLK), .clr(RST));
  Register #(.width(32)) register_29 (.D(WriteData), .en(decoder_11_out1), .Q(register_29_q), .clk(CLK), .clr(RST));
  Register #(.width(32)) register_30 (.D(WriteData), .en(decoder_11_out2), .Q(register_30_q), .clk(CLK), .clr(RST));
  Register #(.width(32)) register_31 (.D(WriteData), .en(decoder_11_out3), .Q(register_31_q), .clk(CLK), .clr(RST));
  Multiplexer #(.select(2), .width(32), .enable("false")) multiplexer_1 (
    .in0({32{1'b0}}), .in1(register_1_q), .in2(register_2_q), .in3(register_3_q), .out(multiplexer_1_out),
    .sel(ReadReg1[1:0]));
  Multiplexer #(.select(2), .width(32), .enable("false")) multiplexer_2 (
    .in0({32{1'b0}}), .in1(register_1_q), .in2(register_2_q), .in3(register_3_q), .out(multiplexer_2_out),
    .sel(ReadReg2[1:0]));
  Multiplexer #(.select(2), .width(32), .enable("false")) multiplexer_3 (
    .in0(register_4_q), .in1(register_5_q), .in2(register_6_q), .in3(register_7_q), .out(multiplexer_3_out),
    .sel(ReadReg1[1:0]));
  Multiplexer #(.select(2), .width(32), .enable("false")) multiplexer_4 (
    .in0(register_4_q), .in1(register_5_q), .in2(register_6_q), .in3(register_7_q), .out(multiplexer_4_out),
    .sel(ReadReg2[1:0]));
  Multiplexer #(.select(2), .width(32), .enable("false")) multiplexer_5 (
    .in0(register_8_q), .in1(register_9_q), .in2(register_10_q), .in3(register_11_q),
    .out(multiplexer_5_out), .sel(ReadReg1[1:0]));
  Multiplexer #(.select(2), .width(32), .enable("false")) multiplexer_6 (
    .in0(register_8_q), .in1(register_9_q), .in2(register_10_q), .in3(register_11_q),
    .out(multiplexer_6_out), .sel(ReadReg2[1:0]));
  Multiplexer #(.select(2), .width(32), .enable("false")) multiplexer_7 (
    .in0(register_12_q), .in1(register_13_q), .in2(register_14_q), .in3(register_15_q),
    .out(multiplexer_7_out), .sel(ReadReg1[1:0]));
  Multiplexer #(.select(2), .width(32), .enable("false")) multiplexer_8 (
    .in0(register_12_q), .in1(register_13_q), .in2(register_14_q), .in3(register_15_q),
    .out(multiplexer_8_out), .sel(ReadReg2[1:0]));
  Multiplexer #(.select(2), .width(32), .enable("false")) multiplexer_9 (
    .in0(register_16_q), .in1(register_17_q), .in2(register_18_q), .in3(register_19_q),
    .out(multiplexer_9_out), .sel(ReadReg1[1:0]));
  Multiplexer #(.select(2), .width(32), .enable("false")) multiplexer_10 (
    .in0(register_16_q), .in1(register_17_q), .in2(register_18_q), .in3(register_19_q),
    .out(multiplexer_10_out), .sel(ReadReg2[1:0]));
  Multiplexer #(.select(2), .width(32), .enable("false")) multiplexer_11 (
    .in0(register_20_q), .in1(register_21_q), .in2(register_22_q), .in3(register_23_q),
    .out(multiplexer_11_out), .sel(ReadReg1[1:0]));
  Multiplexer #(.select(2), .width(32), .enable("false")) multiplexer_12 (
    .in0(register_20_q), .in1(register_21_q), .in2(register_22_q), .in3(register_23_q),
    .out(multiplexer_12_out), .sel(ReadReg2[1:0]));
  Multiplexer #(.select(2), .width(32), .enable("false")) multiplexer_13 (
    .in0(register_24_q), .in1(register_25_q), .in2(register_26_q), .in3(register_27_q),
    .out(multiplexer_13_out), .sel(ReadReg1[1:0]));
  Multiplexer #(.select(2), .width(32), .enable("false")) multiplexer_14 (
    .in0(register_24_q), .in1(register_25_q), .in2(register_26_q), .in3(register_27_q),
    .out(multiplexer_14_out), .sel(ReadReg2[1:0]));
  Multiplexer #(.select(2), .width(32), .enable("false")) multiplexer_15 (
    .in0(register_28_q), .in1(register_29_q), .in2(register_30_q), .in3(register_31_q),
    .out(multiplexer_15_out), .sel(ReadReg1[1:0]));
  Multiplexer #(.select(2), .width(32), .enable("false")) multiplexer_16 (
    .in0(register_28_q), .in1(register_29_q), .in2(register_30_q), .in3(register_31_q),
    .out(multiplexer_16_out), .sel(ReadReg2[1:0]));
  Multiplexer #(.select(2), .width(32), .enable("false")) multiplexer_17 (
    .in0(multiplexer_1_out), .in1(multiplexer_3_out), .in2(multiplexer_5_out), .in3(multiplexer_7_out),
    .out(multiplexer_17_out), .sel(ReadReg1[3:2]));
  Multiplexer #(.select(2), .width(32), .enable("false")) multiplexer_18 (
    .in0(multiplexer_2_out), .in1(multiplexer_4_out), .in2(multiplexer_6_out), .in3(multiplexer_8_out),
    .out(multiplexer_18_out), .sel(ReadReg2[3:2]));
  Multiplexer #(.select(2), .width(32), .enable("false")) multiplexer_19 (
    .in0(multiplexer_9_out), .in1(multiplexer_11_out), .in2(multiplexer_13_out), .in3(multiplexer_15_out),
    .out(multiplexer_19_out), .sel(ReadReg1[3:2]));
  Multiplexer #(.select(2), .width(32), .enable("false")) multiplexer_20 (
    .in0(multiplexer_10_out), .in1(multiplexer_12_out), .in2(multiplexer_14_out), .in3(multiplexer_16_out),
    .out(multiplexer_20_out), .sel(ReadReg2[3:2]));
  Multiplexer #(.width(32), .enable("false")) multiplexer_21 (
    .in0(multiplexer_17_out), .in1(multiplexer_19_out), .out(ReadData1), .sel(ReadReg1[4]));
  Multiplexer #(.width(32), .enable("false")) multiplexer_22 (
    .in0(multiplexer_18_out), .in1(multiplexer_20_out), .out(ReadData2), .sel(ReadReg2[4]));
endmodule
